# Fritzing sketch Schematic (saved by Fritzing 0.9.3b)

parts:
  MOTOR_FR_MOSFET = Basic FET N-Channel [package="D2Pak [SMD]"]
  MOTOR_FL_MOSFET = Basic FET N-Channel [package="D2Pak [SMD]"]
  MOTOR_RL_MOSFET = Basic FET N-Channel [package="D2Pak [SMD]"]
  MOTOR_RR_MOSFET = Basic FET N-Channel [package="D2Pak [SMD]"]
  Powerboost_1000 = PowerBoost 1000 Basic
  3_8V = LIPO-110mAh [package=lipo-110]
  MOTOR_FR = DC Motor
  MOTOR_FL = DC Motor
  MOTOR_RR = DC Motor
  MOTOR_RL = DC Motor
  ICM20948 = Adafruit ICM20948
  ESP32 = Arduino Nano ESP32
  USB-C = USB-C plug

nets:
  N1: MOTOR_FR_MOSFET.Gate, ESP32.Pin_23
  N2: MOTOR_FR_MOSFET.drain, MOTOR_FR.pin_2
  GND: MOTOR_FR_MOSFET.source, MOTOR_FL_MOSFET.source, MOTOR_RL_MOSFET.source, MOTOR_RR_MOSFET.source, ICM20948.GND, ESP32.Pin_14, ESP32.Pin_19, USB-C.GND
  N3: MOTOR_FL_MOSFET.Gate, ESP32.Pin_20
  N4: MOTOR_FL_MOSFET.drain, MOTOR_FL.pin_2
  N5: MOTOR_RL_MOSFET.Gate, ESP32.Pin_21
  N6: MOTOR_RL_MOSFET.drain, MOTOR_RL.pin_2
  N7: MOTOR_RR_MOSFET.Gate, ESP32.Pin_22
  N8: MOTOR_RR_MOSFET.drain, MOTOR_RR.pin_2
  N9: Powerboost_1000.GND, 3_8V.-
  N10: Powerboost_1000.5.0V, USB-C.VCC
  N11: Powerboost_1000.VBAT, 3_8V.+, MOTOR_FR.pin_1, MOTOR_FL.pin_1, MOTOR_RR.pin_1, MOTOR_RL.pin_1
  N12: ICM20948.SCK/SCL, ESP32.Pin_9
  N13: ICM20948.VIN, ESP32.Pin_2
  N14: ICM20948.SDI/SDA, ESP32.Pin_8

custom parts:
  PowerBoost 1000 Basic: The PowerBoost 1000 is a little DC/DC boost converter module that can run from 1.8V batteries or higher, and convert the battery output to 5.2V DC for running your 5V projects. At its heart is a TPS61030 boost converter from TI. This boost converter chip has some really nice extras such as low battery detection, 4A internal switch, synchronous conversion, excellent efficiency, and 700KHz high-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
  Arduino Nano ESP32: Arduino® Nano ESP32 tht.
  USB-C plug: power plug
